# Fritzing sketch Untitled Sketch 2 (saved by Fritzing 0.9.3b)
breadboards: 1

parts:
  LCD1 = LCD screen
  R7 = Rotary Potentiometer (Large) [maximum_resistance=100kΩ package=THT]
  Part1 = Arduino Uno (Rev3)
  VCC2 = 4 x AAA Battery Mount
  J1 = Camdenboss CTB0158-8 [part_number=CTB0158-8 package=THT]
  J2 = Camdenboss CTB0158-2 [part_number=CTB0158-2 package=THT]
  R1 = Resistor [tolerance=±5% resistance=2.2k package=THT]
  R3 = Resistor [tolerance=±5% resistance=2.2k package=THT]
  R4 = Resistor [tolerance=±5% resistance=2.2k package=THT]
  R5 = Resistor [tolerance=±5% resistance=15k package=THT]
  R6 = Resistor [tolerance=±5% resistance=10k package=THT]
  R7_2 = Resistor [tolerance=±5% resistance=4.7k package=THT]
  R8 = Resistor [tolerance=±5% resistance=1k package=THT]
  R2 = Resistor [tolerance=±5% resistance=2.2k package=THT]

nets:
  N1: LCD1.VSS, LCD1.LED+, R7.leg2, VCC2.+, J2.terminal_2, R5.Pin_0, R6.Pin_0, R7_2.Pin_0, R8.Pin_0
  N2: LCD1.VDD, LCD1.R/W, LCD1.LED-, R7.leg1, VCC2.-, J2.terminal_1, R1.Pin_0, R3.Pin_0, R4.Pin_0, R2.Pin_1
  N3: LCD1.V0, R7.wiper
  N4: LCD1.RS, Part1.D12/MISO
  N5: LCD1.E, Part1.D11_PWM/MOSI
  N6: LCD1.DB4, Part1.D5_PWM
  N7: LCD1.DB5, Part1.D4
  N8: LCD1.DB6, Part1.D3_PWM
  N9: LCD1.DB7, Part1.D2
  N10: Part1.A0, J1.terminal_8, R1.Pin_1
  N11: Part1.A1, J1.terminal_7, R2.Pin_0
  N12: Part1.A2, J1.terminal_6, R3.Pin_1
  N13: Part1.A3, J1.terminal_5, R4.Pin_1
  N14: J1.terminal_1, R8.Pin_1
  N15: J1.terminal_2, R7_2.Pin_1
  N16: J1.terminal_3, R6.Pin_1
  N17: J1.terminal_4, R5.Pin_1

// code stored in the sketch: Untitled4.ino
2.2?
